# Fritzing sketch synthio_tutorial_wiring1_full (saved by Fritzing 1.0.4)
breadboards: 1

parts:
  Mod1 = Raspberry Pi Pico
  A1 = Pcm5102A module
  R1 = Rotary Potentiometer (Small) [maximum_resistance=10kΩ knob_status=50% power=0.5W package=THT]
  R2 = Rotary Potentiometer (Small) [maximum_resistance=10kΩ knob_status=50% power=0.5W package=THT]
  S1 = Pushbutton [package="[THT]"]

nets:
  N1: Mod1.pin_3, Mod1.pin_8, Mod1.pin_13, Mod1.pin_18, Mod1.pin_23, Mod1.pin_28, Mod1.pin_33, Mod1.pin_38, Mod1.pin_42, A1.Pin_1, A1.Pin_5, R1.leg1, R2.leg1, S1.Pin_3
  N2: Mod1.pin_26, A1.Pin_2
  N3: Mod1.pin_27, A1.Pin_4
  N4: Mod1.pin_29, A1.Pin_3
  N5: Mod1.pin_31, R1.wiper
  N6: Mod1.pin_32, R2.wiper
  N7: Mod1.pin_34, S1.Pin_1, S1.Pin_2
  N8: Mod1.pin_36, R1.leg2, R2.leg2
  N9: Mod1.pin_39, A1.Pin_6

notes:
  knobB
  knobA
  button
  audio out

custom parts:
  Raspberry Pi Pico: Raspberry Pi Pico. Based around the RP2040 microcontroller the Pico is a low cost microcontroller device bringing Raspberry Pi quality, cost, and easy of use to the microcontroller space. Jan 2021, Split part in to two versions: tht (this one) and SMD. This one will drill holes for a .1 in header in pcb to allow plugging in the module as well as providing pads to solder the module to the top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
  Pcm5102A module: Interface I2S PCM5102A DAC Decoder GY-PCM5102 I2S Player Module for Raspberry Pi pHAT Format Board Digital PCM5102 Audio Board.
